// Digital circuit CU.dig as structural Verilog
module CU (
  input  Start,
  input  S,
  input  Reset,
  input  Clk,
  output T0,
  output T1,
  output T2,
  output T3,
  output T4
);

  wire and_1_out, and_2_out, and_3_out, and_4_out, and_5_out, or_1_out, or_2_out, or_3_out;

  and and_1 (and_1_out, ~Start, or_2_out);  // And
  and and_2 (and_2_out, ~S, T3);  // And
  or or_1 (or_1_out, and_1_out, and_2_out);
  and and_3 (and_3_out, Start, T0);
  or or_2 (or_2_out, T4, T0);
  D_FF_AS d_ff_as_1 (.Set(~Reset), .D(or_1_out), .C(Clk), .Clr(~1'b1), .Q(T0));  // open: nQ
  and and_4 (and_4_out, Start, T4);
  and and_5 (and_5_out, S, T3);
  D_FF_AS d_ff_as_2 (.Set(~1'b1), .D(and_3_out), .C(Clk), .Clr(~Reset), .Q(T1));  // open: nQ
  or or_3 (or_3_out, and_4_out, and_5_out);
  D_FF_AS d_ff_as_3 (.Set(~1'b1), .D(T1), .C(Clk), .Clr(~Reset), .Q(T2));  // open: nQ
  D_FF_AS d_ff_as_4 (.Set(~1'b1), .D(T2), .C(Clk), .Clr(~Reset), .Q(T3));  // open: nQ
  D_FF_AS d_ff_as_5 (.Set(~1'b1), .D(or_3_out), .C(Clk), .Clr(~Reset), .Q(T4));  // open: nQ
endmodule
