// Digital circuit Modified_CU.dig as structural Verilog
module Modified_CU (
  input  Start,
  input  S,
  input  Reset,
  input  Clk,
  input  Halt_T1,
  input  Halt_T2,
  input  Halt_T3,
  input  Halt_T4,
  output T0,
  output T1,
  output T2,
  output T3,
  output T4
);

  wire a2, and_1_out, and_2_out, and_3_out, and_4_out, and_5_out, and_7_out, and_8_out, and_9_out,
       and_10_out, and_11_out, and_12_out, D0, or_2_out, or_3_out, or_4_out, or_5_out;

  and and_1 (and_1_out, ~Start, T4, ~Halt_T4);  // And
  and and_2 (and_2_out, ~S, T3);  // And
  and and_3 (and_3_out, Start, T0);
  or or_1 (D0, and_1_out, 1'b0, and_2_out);
  and and_4 (and_4_out, Start, T4);
  D_FF_AS d_ff_as_1 (.Set(~Reset), .D(D0), .C(Clk), .Clr(~1'b1), .Q(T0));  // open: nQ
  and and_5 (and_5_out, ~Start, T0);  // And
  and and_6 (a2, T1, Halt_T1);
  or or_2 (or_2_out, and_3_out, and_5_out, a2);
  D_FF_AS d_ff_as_2 (.Set(~1'b1), .D(or_2_out), .C(Clk), .Clr(~Reset), .Q(T1));  // open: nQ
  and and_7 (and_7_out, ~Halt_T1, T1);  // And
  or or_3 (or_3_out, and_7_out, and_8_out);
  and and_8 (and_8_out, Halt_T2, T2);
  D_FF_AS d_ff_as_3 (.Set(~1'b1), .D(or_3_out), .C(Clk), .Clr(~Reset), .Q(T2));  // open: nQ
  and and_9 (and_9_out, ~Halt_T3, S, T3);  // And
  and and_10 (and_10_out, ~Halt_T2, T2);  // And
  and and_11 (and_11_out, Halt_T4, T4);
  or or_4 (or_4_out, and_10_out, and_12_out);
  or or_5 (or_5_out, and_4_out, and_9_out, and_11_out);
  D_FF_AS d_ff_as_4 (.Set(~1'b1), .D(or_4_out), .C(Clk), .Clr(~Reset), .Q(T3));  // open: nQ
  and and_12 (and_12_out, T3, Halt_T3);
  D_FF_AS d_ff_as_5 (.Set(~1'b1), .D(or_5_out), .C(Clk), .Clr(~Reset), .Q(T4));  // open: nQ

  // Notes on the sheet:
  //   Reset: default 1
endmodule
