// Digital circuit Modified_system.dig as structural Verilog
module Modified_system (
  input  X0,
  input  X1,
  input  X2,
  input  X3,
  input  CLK,
  input  Start,
  input  Halt_T1,
  input  Halt_T2,
  input  Halt_T3,
  input  Halt_T4,
  output Z0,
  output Z1,
  output Z2,
  output Z3
);

  wire _1bit_reg_1_p5, _1bit_reg_2_p5, _4bit_reg_loadcontrol_1_p5, _4bit_reg_loadcontrol_1_p7,
       _4bit_reg_loadcontrol_1_p9, _4bit_reg_loadcontrol_1_p11, modified_cu_1_t0, modified_cu_1_t1,
       modified_cu_1_t2, modified_cu_1_t3, or_1_out, Reset_out, T4;

  Button #(.activeLow("true")) Reset (.out(Reset_out));
  Modified_CU modified_cu_1 (
    .Start(Start), .S(_1bit_reg_1_p5), .Reset(Reset_out), .Clk(CLK), .Halt_T1(Halt_T1), .Halt_T2(Halt_T2),
    .Halt_T3(Halt_T3), .Halt_T4(Halt_T4), .T0(modified_cu_1_t0), .T1(modified_cu_1_t1),
    .T2(modified_cu_1_t2), .T3(modified_cu_1_t3), .T4(T4));
  LED led_1 (.in(modified_cu_1_t0));
  LED led_2 (.in(modified_cu_1_t1));
  LED led_3 (.in(modified_cu_1_t2));
  LED led_4 (.in(modified_cu_1_t3));
  LED led_5 (.in(T4));
  // _4bit_reg_loadcontrol _4bit_reg_loadcontrol_1: pin names not known; wires that end beside it: modified_cu_1_t1, Reset_out, X3, X2, _4bit_reg_loadcontrol_1_p5, X1, _4bit_reg_loadcontrol_1_p7, X0, _4bit_reg_loadcontrol_1_p9, CLK, _4bit_reg_loadcontrol_1_p11
  or or_1 (or_1_out, _4bit_reg_loadcontrol_1_p11, _4bit_reg_loadcontrol_1_p5);
  // _1bit_reg _1bit_reg_1: pin names not known; wires that end beside it: or_1_out, modified_cu_1_t2, CLK, Reset_out, _1bit_reg_1_p5
  // _4bit_reg_loadcontrol _4bit_reg_loadcontrol_2: pin names not known; wires that end beside it: T4, Reset_out, _4bit_reg_loadcontrol_1_p5, _4bit_reg_loadcontrol_1_p7, Z3, _4bit_reg_loadcontrol_1_p9, Z2, _4bit_reg_loadcontrol_1_p11, Z1, CLK, Z0
  // _1bit_reg _1bit_reg_2: pin names not known; wires that end beside it: T4, 1'b1, CLK, 1'b1, _1bit_reg_2_p5
  LED Ready (.in(_1bit_reg_2_p5));
endmodule
